# Fritzing sketch nato-lights (saved by Fritzing 0.9.6b)
circuit board: 6cm x 7.5cm
stripboards: 1

parts:
  part = Rotary Potentiometer (Large) [maximum_resistance=100kΩ package=THT]
  BTN = Pushbutton [package="[SMD]"]
  part_2 = Resistor [tolerance=±5% power=0.25 resistance=10000 package=THT]
  CH2 = Resistor [tolerance=±5% power=0.25 resistance=330 package=THT]
  CH3 = Resistor [tolerance=±5% power=0.25 resistance=330 package=THT]
  CH1 = Resistor [tolerance=±5% power=0.25 resistance=330 package=THT]
  part_3 = Arduino Uno (Rev3)

nets:
  N1: part.leg1, part_2.Pin_0, part_3.GND
  N2: part.wiper, part_3.A0
  N3: part.leg2, BTN.Pin_1, BTN.Pin_2, part_3.5V
  N4: BTN.Pin_3, BTN.Pin_4, part_2.Pin_1, part_3.D4
  N5: CH2.Pin_1, part_3.D5_PWM
  N6: CH3.Pin_1, part_3.D3_PWM
  N7: CH1.Pin_1, part_3.D6_PWM

notes:
  5V
  GND
  CH1
  CH2
  CH3

// code stored in the sketch: nato-lights.ino
#include "src/common.h"
#include "src/lights.h"
#include "src/pattern.h"
#include "src/patterns/pattern_colors.h"
#include "src/patterns/pattern_fire.h"
#include "src/patterns/pattern_trains.h"
#include "src/patterns/pattern_white.h"

unsigned long debounce;
CRGB leds[LED_BUFFER_SIZE];
LightsControl Lights;
HardwareControl Hardware;

void show(unsigned char strip, unsigned short offset, unsigned short count) {
  for (signed short i = LED_COUNT - 1; i >= offset + count; i--) {
    leds[i + LED_BUFFER_PADDING] = leds[i];
  }

  for (signed short i = count - 1; i >= 0; i--) {
    for (unsigned char j = 0; j < LED_DUPLICATION; j++) {
      leds[i * LED_DUPLICATION + j + offset] = leds[i + offset];
    }
  }

  FastLED[strip].showLeds();

  for (unsigned short i = 0; i < count; i++) {
    leds[i + offset] = leds[i * LED_DUPLICATION + offset];
  }

  for (unsigned short i = offset + count; i < LED_COUNT; i++) {
    leds[i] = leds[i + LED_BUFFER_PADDING];
  }
}

void setup() {
#ifdef DEBUG
  Serial.begin(9600);
#endif

  FastLED.addLeds<LED_TYPE, LED_PIN_1>(leds, LED_OFFSET_1, LED_COUNT_1 * LED_DUPLICATION);
  FastLED.addLeds<LED_TYPE, LED_PIN_2>(leds, LED_OFFSET_2, LED_COUNT_2 * LED_DUPLICATION);
  FastLED.addLeds<LED_TYPE, LED_PIN_3>(leds, LED_OFFSET_3, LED_COUNT_3 * LED_DUPLICATION);
  Lights = LightsControl();
  Lights.addPattern<PatternWhite>();
  Lights.addPattern<PatternColors>();
  Lights.addPattern<PatternFire>();
  Lights.addPattern<PatternTrains>();
  Hardware = HardwareControl();
}

void loop() {
  Lights.step();
  show(0, LED_OFFSET_1, LED_COUNT_1);
  show(1, LED_OFFSET_2, LED_COUNT_2);
  show(2, LED_OFFSET_3, LED_COUNT_3);
  delay(1);

  if (Hardware.getNextButtonPressed()) {
    Lights.nextPattern();
  }
}
